// Logisim project design.circ as structural Verilog: 2 circuits, main circuit main
module main (
);

  wire ADC_out, ADD_2_out, ADD_out, adder_5_cout, and_1_out, and_2_out, and_3_out, and_4_out, and_5_out,
       and_6_out, and_7_out, and_8_out, and_9_out, and_10_out, and_11_out, and_12_out, and_13_out,
       and_14_out, and_15_out, and_16_out, Bit_2_out, Bit_3_out, Bit_4_out, Bit_5_out, Bit_out, buffer_1_out,
       buffer_2_out, buffer_3_out, C_2_out, C_out, CALL_out, Carry_flag_q, CF_out, Clear_out, Clock_2_out,
       Clock_3_out, Clock_out, decoder_1_out0, decoder_1_out1, decoder_1_out2, decoder_1_out3,
       decoder_2_out1, decoder_2_out2, decoder_2_out3, decoder_2_out4, decoder_2_out5, decoder_2_out6,
       decoder_2_out7, decoder_2_out8, decoder_2_out9, decoder_2_out10, decoder_2_out11, decoder_2_out12,
       decoder_2_out13, decoder_2_out14, decoder_2_out15, decoder_2_out16, decoder_2_out17, decoder_2_out18,
       decoder_2_out19, decoder_2_out20, decoder_2_out22, decoder_2_out24, decoder_2_out25, decoder_2_out31,
       Enable_2_out, ENABLE_3_out, ENABLE_4_out, ENABLE_5_out, ENABLE_6_out, Enable_out, Halted_qn, JA_2_out,
       JA_out, JC_out, JMP_2_out, JMP_3_out, JMP_4_out, JMP_5_out, JMP_6_out, JMP_out, JNA_2_out, JNA_out,
       JNC_out, JNZ_out, JZ_out, multiplexer_10_out, NO_CMP_out, not_1_out, not_2_out, not_3_out, not_4_out,
       not_6_out, not_7_out, not_8_out, not_9_out, not_11_out, not_12_out, Reset_out, RET_out, S_C_out,
       SBB_out, SEL_out, SR_out, Stack_prime_out, SUB_out, SW_out, Write_2_out, Write_out, Zero_2_out,
       Zero_3_out, Zero_4_out, Zero_5_out, Zero_6_out, Zero_7_out, Zero_flag_q, Zero_out, ZF_out;
  wire [1:0] adder_2_out, Address_out, Data_byte_q_2, decoder_2_out21, Low_out, Step_q;
  wire [2:0] multiplexer_8_out, n3_bit_dedecoder_1_out_8;
  wire [6:0] keyboard_1_data;
  wire [7:0] A_q, adder_1_out, adder_3_out, adder_4_out, adder_5_out, adder_6_out, and_17_out, B_q,
       Data_byte_q, Instruction_byte_q, Instruction_pointer_q, multiplexer_1_out, multiplexer_2_out,
       multiplexer_3_out, multiplexer_4_out, multiplexer_6_out, multiplexer_7_out, multiplexer_9_out,
       multiplexer_11_out, multiplexer_12_out, multiplexer_13_out, not_5_out, not_10_out, or_1_out,
       ram_1_data, shifter_1_out, shifter_2_out, Stack_pointer_q, xor_1_out;
  wire [7:3] multiplexer_8_out_2;

  Clock Clock (.out(Clock_out));
  Button Reset (.out(Reset_out));
  and SEL (SEL_out, Instruction_byte_q[2], RET_out);
  Multiplexer #(.width(8), .enable("false")) multiplexer_1 (
    .in0(8'h1), .in1({multiplexer_8_out_2, multiplexer_8_out}), .out(multiplexer_1_out), .sel(SEL_out));
  D_Flip_Flop Halted (
    .clk(decoder_2_out31), .D(decoder_2_out31), .Qn(Halted_qn), .reset(Reset_out));  // open: Q, preset, en
  and Clock_2 (Clock_2_out, Halted_qn, Clock_out);
  and ADD (ADD_out, not_2_out, RET_out);
  Adder adder_1 (.a(Instruction_pointer_q), .b(multiplexer_1_out), .out(adder_1_out));  // open: cin, cout
  not not_1 (not_1_out, decoder_1_out2);
  not not_2 (not_2_out, Instruction_byte_q[2]);
  Register Instruction_pointer (
    .D(multiplexer_2_out), .en(Enable_out), .Q(Instruction_pointer_q), .clk(Clock_2_out), .clr(Reset_out));
  Multiplexer #(.width(8), .enable("false")) multiplexer_2 (
    .in0(adder_1_out), .in1({multiplexer_8_out_2, multiplexer_8_out}), .out(multiplexer_2_out), .sel(ADD_out));
  or Enable (Enable_out, RET_out, not_1_out);
  Register #(.width(2)) Step (.D(adder_2_out), .Q(Step_q), .clk(Clock_2_out), .clr(Clear_out));  // open: en
  Adder #(.width(2)) adder_2 (.a(Step_q), .b(2'b01), .out(adder_2_out));  // open: cin, cout
  or Clear (Clear_out, Reset_out, decoder_1_out3);
  Multiplexer #(.width(8), .enable("false")) multiplexer_3 (
    .in0({8{1'b1}}), .in1(8'h1), .out(multiplexer_3_out), .sel(SR_out));
  Multiplexer #(.select(2), .width(8), .enable("false")) multiplexer_4 (
    .in0(Instruction_pointer_q), .in1(multiplexer_7_out), .in2(Stack_pointer_q), .in3(adder_3_out),
    .out(multiplexer_4_out), .sel(Address_out));
  Decoder #(.select(2), .disabled(0), .enable("false")) decoder_1 (
    .out0(decoder_1_out0), .out1(decoder_1_out1), .out2(decoder_1_out2), .out3(decoder_1_out3), .sel(Step_q));
  Adder adder_3 (.a(Stack_pointer_q), .b(multiplexer_3_out), .out(adder_3_out));  // open: cin, cout
  or Write (Write_out, SW_out, decoder_2_out2);
  or SW (SW_out, decoder_2_out21[0], decoder_2_out21[1]);
  or SR (SR_out, decoder_2_out22, decoder_2_out24);
  or Stack_prime (Stack_prime_out, SR_out, SW_out);
  and and_1 (and_1_out, multiplexer_4_out[0], multiplexer_4_out[1]);
  and and_2 (and_2_out, multiplexer_4_out[2], multiplexer_4_out[3]);
  and and_3 (and_3_out, multiplexer_4_out[4], multiplexer_4_out[5]);
  and and_4 (and_4_out, multiplexer_4_out[6], multiplexer_4_out[7]);
  RAM ram_1 (
    .addr(multiplexer_4_out), .data(ram_1_data), .clk(Clock_2_out), .ld(Write_2_out), .clr(Reset_out));  // open: sel
  nor Write_2 (Write_2_out, Write_out, and_16_out);
  Multiplexer #(.select(2), .width(8)) multiplexer_5 (
    .in0(multiplexer_12_out), .in1({multiplexer_8_out_2, multiplexer_8_out}), .in2(Instruction_pointer_q),
    .out(ram_1_data), .sel(decoder_2_out21), .en(Write_out));  // open: in3
  Adder adder_4 (.a(adder_3_out), .b(multiplexer_7_out), .out(adder_4_out));  // open: cin, cout
  or Stack_prime_2 (Address_out[1], decoder_2_out25, Stack_prime_out);
  not not_3 (not_3_out, multiplexer_4_out[0]);
  and and_5 (and_5_out, not_3_out, multiplexer_4_out[1]);
  and and_6 (and_6_out, multiplexer_4_out[2], multiplexer_4_out[3]);
  and and_7 (and_7_out, multiplexer_4_out[4], multiplexer_4_out[5]);
  and and_8 (and_8_out, multiplexer_4_out[6], multiplexer_4_out[7]);
  and and_9 (and_9_out, and_1_out, and_2_out);
  and and_10 (and_10_out, and_9_out, and_11_out);
  and and_11 (and_11_out, and_3_out, and_4_out);
  and and_12 (and_12_out, and_10_out, Write_out);
  Multiplexer #(.select(2), .width(8), .enable("false")) multiplexer_6 (
    .in0(adder_3_out), .in1(8'hfd), .in2(adder_4_out), .in3({multiplexer_8_out_2, multiplexer_8_out}),
    .out(multiplexer_6_out), .sel(Low_out));
  or High (Low_out[1], decoder_2_out25, decoder_2_out24);
  or Enable_2 (Enable_2_out, Address_out[1], Reset_out);
  or Low (Low_out[0], decoder_2_out25, Reset_out);
  and and_13 (and_13_out, and_5_out, and_6_out);
  and and_14 (and_14_out, and_7_out, and_8_out);
  TTY tty_1 (.data(ram_1_data[6:0]), .clk(Clock_2_out), .we(and_12_out), .clr(Reset_out));
  Register Instruction_byte (
    .D(ram_1_data), .en(decoder_1_out0), .Q(Instruction_byte_q), .clk(Clock_2_out), .clr(Reset_out));
  Register Data_byte (
    .D(ram_1_data), .en(decoder_1_out1), .Q({Data_byte_q_2, Data_byte_q[7], Data_byte_q[4:0]}),
    .clk(Clock_2_out), .clr(Reset_out));
  Multiplexer #(.width(8), .enable("false")) multiplexer_7 (
    .in0({Data_byte_q_2, Data_byte_q[7], Data_byte_q[4:0]}), .in1(adder_6_out), .out(multiplexer_7_out),
    .sel(Instruction_byte_q[0]));
  Register Stack_pointer (
    .D(multiplexer_6_out), .en(Enable_2_out), .Q(Stack_pointer_q), .clk(Clock_3_out));  // open: clr
  or Clock_3 (Clock_3_out, Clock_2_out, buffer_1_out);
  buf buffer_1 (buffer_1_out, buffer_2_out);
  buf buffer_2 (buffer_2_out, buffer_3_out);
  buf buffer_3 (buffer_3_out, Reset_out);
  and and_15 (and_15_out, and_13_out, and_14_out);
  not not_4 (not_4_out, Write_out);
  and Address (Address_out[0], decoder_1_out2, Instruction_byte_q[1]);
  Keyboard keyboard_1 (.clk(Clock_2_out), .re(and_16_out), .clr(Reset_out), .data(keyboard_1_data));  // open: avail
  and and_16 (and_16_out, and_15_out, not_4_out);
  assign ram_1_data = and_16_out ? {1'b0, keyboard_1_data} : 8'bz;  // Controlled_Buffer controlled_buffer_1
  Multiplexer #(.select(2), .width(8), .enable("false")) multiplexer_8 (
    .in0({Data_byte_q_2, Data_byte_q[7], Data_byte_q[4:0]}), .in1(adder_6_out), .in2(ram_1_data),
    .in3(ram_1_data), .out({multiplexer_8_out_2, multiplexer_8_out}), .sel(Instruction_byte_q[1:0]));
  Decoder #(.select(5), .disabled(0)) decoder_2 (
    .out1(decoder_2_out1), .out2(decoder_2_out2), .out3(decoder_2_out3), .out4(decoder_2_out4),
    .out5(decoder_2_out5), .out6(decoder_2_out6), .out7(decoder_2_out7), .out8(decoder_2_out8),
    .out9(decoder_2_out9), .out10(decoder_2_out10), .out11(decoder_2_out11), .out12(decoder_2_out12),
    .out13(decoder_2_out13), .out14(decoder_2_out14), .out15(decoder_2_out15), .out16(decoder_2_out16),
    .out17(decoder_2_out17), .out18(decoder_2_out18), .out19(decoder_2_out19), .out20(decoder_2_out20),
    .out21(decoder_2_out21[0]), .out22(decoder_2_out22), .out23(decoder_2_out21[1]), .out24(decoder_2_out24),
    .out25(decoder_2_out25), .out31(decoder_2_out31), .sel(Instruction_byte_q[7:3]), .en(decoder_1_out2));  // open: out0, out26, out27, out28, out29, out30
  or S_C (S_C_out, decoder_2_out5, decoder_2_out7);
  or SUB (SUB_out, decoder_2_out6, S_C_out);
  or ADD_2 (ADD_2_out, decoder_2_out3, decoder_2_out4);
  or CF (CF_out, ADD_2_out, SUB_out);
  or ZF (ZF_out, CF_out, Bit_5_out);
  or Bit (Bit_out, decoder_2_out8, decoder_2_out9);
  or Bit_2 (Bit_2_out, Bit_out, decoder_2_out10);
  or Bit_3 (Bit_3_out, Bit_2_out, decoder_2_out11);
  or Bit_4 (Bit_4_out, Bit_3_out, decoder_2_out12);
  or Bit_5 (Bit_5_out, Bit_4_out, decoder_2_out13);
  or ENABLE_3 (ENABLE_3_out, ZF_out, decoder_2_out1);
  _3_bit_dedecoder u_3_bit_dedecoder_1 (
    .in_1(CF_out), .in_2(decoder_2_out8), .in_3(decoder_2_out9), .in_4(decoder_2_out10),
    .in_5(decoder_2_out11), .in_6(decoder_2_out12), .in_7(decoder_2_out13), .out_8(n3_bit_dedecoder_1_out_8));
  assign not_5_out = ~{multiplexer_8_out_2, multiplexer_8_out};  // NOT_Gate not_5, 8 bits wide
  not not_6 (not_6_out, decoder_2_out7);
  or ENABLE_4 (ENABLE_4_out, decoder_2_out22, ENABLE_3_out);
  nor Zero (Zero_out, multiplexer_11_out[0], multiplexer_11_out[1]);
  nor Zero_2 (Zero_2_out, multiplexer_11_out[2], multiplexer_11_out[3]);
  nor Zero_3 (Zero_3_out, multiplexer_11_out[4], multiplexer_11_out[5]);
  nor Zero_4 (Zero_4_out, multiplexer_11_out[6], multiplexer_11_out[7]);
  and JC (JC_out, decoder_2_out15, Carry_flag_q);
  and JNC (JNC_out, decoder_2_out16, not_7_out);
  not not_7 (not_7_out, Carry_flag_q);
  and JZ (JZ_out, decoder_2_out17, Zero_flag_q);
  and JNZ (JNZ_out, decoder_2_out18, not_8_out);
  not not_8 (not_8_out, Zero_flag_q);
  not not_9 (not_9_out, Carry_flag_q);
  or C (C_out, S_C_out, C_2_out);
  Multiplexer #(.width(8), .enable("false")) multiplexer_9 (
    .in0({multiplexer_8_out_2, multiplexer_8_out}), .in1(not_5_out), .out(multiplexer_9_out), .sel(SUB_out));
  and NO_CMP (NO_CMP_out, not_6_out, ENABLE_4_out);
  and Zero_5 (Zero_5_out, Zero_out, Zero_2_out);
  and Zero_6 (Zero_6_out, Zero_3_out, Zero_4_out);
  or JMP (JMP_out, decoder_2_out14, JC_out);
  and ADC (ADC_out, Carry_flag_q, decoder_2_out4);
  or C_2 (C_2_out, ADC_out, SBB_out);
  and SBB (SBB_out, not_9_out, decoder_2_out6);
  Adder adder_5 (.a(multiplexer_12_out), .b(multiplexer_9_out), .out(adder_5_out), .cin(C_out), .cout(adder_5_cout));
  assign and_17_out = multiplexer_12_out & {multiplexer_8_out_2, multiplexer_8_out};  // AND_Gate and_17, 8 bits wide
  assign or_1_out = multiplexer_12_out | {multiplexer_8_out_2, multiplexer_8_out};  // OR_Gate or_1, 8 bits wide
  assign xor_1_out = multiplexer_12_out ^ {multiplexer_8_out_2, multiplexer_8_out};  // XOR_Gate xor_1, 8 bits wide
  assign not_10_out = ~{multiplexer_8_out_2, multiplexer_8_out};  // NOT_Gate not_10, 8 bits wide
  Shifter shifter_1 (.in(multiplexer_12_out), .\dist (multiplexer_8_out), .out(shifter_1_out));
  Shifter #(.shift("lr")) shifter_2 (.in(multiplexer_12_out), .\dist (multiplexer_8_out), .out(shifter_2_out));
  Multiplexer #(.enable("false")) multiplexer_10 (
    .in0(adder_5_cout), .in1(not_11_out), .out(multiplexer_10_out), .sel(SUB_out));
  not not_11 (not_11_out, adder_5_cout);
  and Zero_7 (Zero_7_out, Zero_5_out, Zero_6_out);
  or JMP_2 (JMP_2_out, JMP_out, JNC_out);
  or JMP_3 (JMP_3_out, JMP_2_out, JZ_out);
  nor JA (JA_out, Carry_flag_q, Zero_flag_q);
  and JA_2 (JA_2_out, JA_out, decoder_2_out19);
  or JNA (JNA_out, Carry_flag_q, Zero_flag_q);
  and JNA_2 (JNA_2_out, JNA_out, decoder_2_out20);
  Multiplexer #(.select(3), .width(8), .enable("false")) multiplexer_11 (
    .in0({multiplexer_8_out_2, multiplexer_8_out}), .in1(adder_5_out), .in2(and_17_out), .in3(or_1_out),
    .in4(xor_1_out), .in5(not_10_out), .in6(shifter_1_out), .in7(shifter_2_out), .out(multiplexer_11_out),
    .sel(n3_bit_dedecoder_1_out_8));
  D_Flip_Flop Carry_flag (
    .clk(Clock_2_out), .D(multiplexer_10_out), .Q(Carry_flag_q), .en(CF_out), .reset(Reset_out));  // open: Qn, preset
  D_Flip_Flop Zero_flag (
    .clk(Clock_2_out), .D(Zero_7_out), .Q(Zero_flag_q), .en(ZF_out), .reset(Reset_out));  // open: Qn, preset
  or JMP_4 (JMP_4_out, JMP_3_out, JNZ_out);
  or JMP_5 (JMP_5_out, JMP_4_out, JA_2_out);
  not not_12 (not_12_out, Instruction_byte_q[2]);
  and ENABLE_5 (ENABLE_5_out, not_12_out, NO_CMP_out);
  and ENABLE_6 (ENABLE_6_out, Instruction_byte_q[2], NO_CMP_out);
  or JMP_6 (JMP_6_out, JMP_5_out, JNA_2_out);
  or CALL (CALL_out, JMP_6_out, decoder_2_out21[1]);
  Register A (.D(multiplexer_11_out), .en(ENABLE_5_out), .Q(A_q), .clk(Clock_2_out), .clr(Reset_out));
  Register B (.D(multiplexer_11_out), .en(ENABLE_6_out), .Q(B_q), .clk(Clock_2_out), .clr(Reset_out));
  or RET (RET_out, CALL_out, decoder_2_out24);
  Multiplexer #(.width(8), .enable("false")) multiplexer_12 (
    .in0(A_q), .in1(B_q), .out(multiplexer_12_out), .sel(Instruction_byte_q[2]));
  Multiplexer #(.select(2), .width(8), .enable("false")) multiplexer_13 (
    .in0(A_q), .in1(B_q), .in2(Instruction_pointer_q), .in3(Stack_pointer_q), .out(multiplexer_13_out),
    .sel(Data_byte_q_2));
  Adder adder_6 (
    .a(multiplexer_13_out), .b({{3{Data_byte_q[7]}}, Data_byte_q[4:0]}), .out(adder_6_out));  // open: cin, cout

  // Notes on the sheet:
  //   The Neva 8-bit Processor
  //   https://github.com/bplaat/neva-processor
  //   Made by Bastiaan van der Plaat
  //   Address - Write - Overwrite Memory
  //   Clock - Reset - Data
endmodule

module _3_bit_dedecoder (
  input  in_1,
  input  in_2,
  input  in_3,
  input  in_4,
  input  in_5,
  input  in_6,
  input  in_7,
  output [2:0] out_8
);

  wire or_1_out, or_2_out, or_3_out, or_4_out, or_5_out, or_6_out;

  or or_1 (or_1_out, in_3, in_1);
  or or_2 (or_2_out, in_3, in_2);
  or or_3 (or_3_out, in_5, in_4);
  or or_4 (or_4_out, or_1_out, in_5);
  or or_5 (or_5_out, or_2_out, in_6);
  or or_6 (or_6_out, or_3_out, in_6);
  or or_7 (out_8[0], in_7, or_4_out);
  or or_8 (out_8[1], in_7, or_5_out);
  or or_9 (out_8[2], in_7, or_6_out);
endmodule
